# Fritzing sketch PillBox (saved by Fritzing 0.9.3b)
breadboards: 1

parts:
  Εξάρτημα1 = Arduino Uno (Rev3)
  U1 = ESP8266 WiFi Module [part_number=ESP8266]
  S1 = Pushbutton [package="[THT]"]
  S2 = Pushbutton [package="[THT]"]
  J1 = Basic Servo

nets:
  N1: Εξάρτημα1.D9_PWM, J1.pulse
  GND: Εξάρτημα1.GND, U1.GND, S1.Pin_3, S1.Pin_4, S2.Pin_3, S2.Pin_4, J1.gnd
  N2: Εξάρτημα1.D0/RX, U1.TX
  N3: Εξάρτημα1.D1/TX, U1.RX
  N4: Εξάρτημα1.D2, S2.Pin_1, S2.Pin_2
  N5: Εξάρτημα1.D4, S1.Pin_1, S1.Pin_2
  3V3: Εξάρτημα1.3V3, U1.3.3V
  5V: Εξάρτημα1.5V, J1.vcc
